# Fritzing sketch circuit (saved by Fritzing 0.8.7b)
breadboards: 1

parts:
  V1 = DC Power [voltage=3.7]
  V2 = DC Power [voltage=3.7]
  Arduino = Arduino Nano (Rev3.0)
  R2 = Resistor [tolerance=±5% resistance=10k package=THT]
  L1 = Inductor [package="400 mil [THT]"]
  D2 = Rectifier Diode [part_number=FMG-G2CS-ND package="300 mil [THT]"]
  R4 = Resistor [tolerance=±5% resistance=10M package=THT]
  R5 = Resistor [tolerance=±5% resistance=10M package=THT]
  R7 = Resistor [tolerance=±5% resistance=10k package=THT]
  Q3 = Basic FET N-Channel [part_number=568-4897-5-ND package="TO220 [THT]"]
  R11 = Resistor [tolerance=±5% resistance=10k package=THT]
  R12 = Resistor [tolerance=±5% resistance=10k package=THT]
  S8 = Pushbutton [package=THT]
  S9 = Pushbutton [package=THT]
  S10 = Pushbutton [package=THT]
  S11 = Pushbutton [package=THT]

nets:
  N1: V1.V+, V2.V-
  GND: V1.V-, Arduino.GND, R2.Pin_1, R5.Pin_1, R7.Pin_1, Q3.source, R11.Pin_1, R12.Pin_1
  N2: V2.V+, S11.leg0
  N3: Arduino.D2, R7.Pin_0, S10.leg0
  N4: Arduino.D6, R11.Pin_0, S8.leg0
  N5: Arduino.D7, R12.Pin_0, S9.leg0
  N6: Arduino.D9, R2.Pin_0, Q3.gate
  N7: Arduino.VIN, L1.pin_0, D2.cathode, R4.Pin_0, S11.leg1
  N8: Arduino.A1, R4.Pin_1, R5.Pin_0
  N9: Arduino.3V3, S8.leg1, S9.leg1, S10.leg1
  N10: L1.pin_1, D2.anode, Q3.drain

notes:
  screen SDA
  screen SCL
  screen
  read V
  read HR
  HR
  HR GND
  screen GND
  Main Power
  Vaporizing Coil
  Watts-
  Watts+
  Activate
  Charge
  PWM
